// Logisim project ORG-04.circ as structural Verilog
module DATAPATH (
  input  [25:0] DOUT_ROM,
  input  [31:0] DOUT_RAM,
  input  CLOCK,
  input  [1:0] SEL_OP1,
  input  SEL_OP2,
  input  WR_ACC,
  output [25:0] GOES_TO_CONTROL,
  output [31:0] DIN_RAM
);

  wire [31:0] bit_extender_1_out, multiplexer_1_out, multiplexer_2_out, ULA_out_3;

  Multiplexer #(.width(32)) multiplexer_1 (
    .in0(DOUT_RAM), .in1(bit_extender_1_out), .out(multiplexer_1_out), .sel(SEL_OP2));  // open: en
  Register #(.width(26)) IR (.D(DOUT_ROM), .Q(GOES_TO_CONTROL), .clk(CLOCK));  // open: en, clr
  ULA ULA (.in_1(DIN_RAM), .in_2(multiplexer_1_out), .out_3(ULA_out_3));
  Multiplexer #(.select(2), .width(32)) multiplexer_2 (
    .in0(DOUT_RAM), .in1(bit_extender_1_out), .in2(ULA_out_3), .out(multiplexer_2_out), .sel(SEL_OP1));  // open: in3, en
  assign bit_extender_1_out = {{6{1'b0}}, GOES_TO_CONTROL};  // Bit_Extender bit_extender_1
  Register #(.width(32)) ACC (.D(multiplexer_2_out), .en(WR_ACC), .Q(DIN_RAM), .clk(CLOCK));  // open: clr

  // Notes on the sheet:
  //   lembrar de dividir a parada ali
endmodule

module ULA (
  input  [31:0] in_1,
  input  [31:0] in_2,
  output [31:0] out_3
);
endmodule

module SIGNAL_EXTENSION (
  input  [25:0] INPUT,
  output [31:0] OUTPUT
);


  assign OUTPUT = {{6{1'b0}}, INPUT};
endmodule

module COMPUTER (
);

  SIGNAL_EXTENSION signal_extension_1 ();  // open: INPUT, OUTPUT
  DATAPATH datapath_1 ();  // open: DOUT_RAM, SEL_OP1, SEL_OP2, WR_ACC, DIN_RAM, DOUT_ROM, GOES_TO_CONTROL, CLOCK
endmodule
